# Fritzing sketch example-bb (saved by Fritzing 0.9.9b)
breadboards: 1

parts:
  Part1 = Arduino Uno (Rev3)
  R1 = Photocell (LDR) [package=THT]
  R2 = Resistor [tolerance=±5% power=0.25 resistance=10k package=THT]
  R3 = Rotary Potentiometer (Small) [maximum_resistance=100kΩ package=THT]
  LED1 = LED - 5mm [color="Red (633nm)" current=0.030 package="5 mm [THT]"]
  R4 = Resistor [tolerance=±5% power=0.25 resistance=470 package=THT]

nets:
  N1: Part1.A0, R1.pin_1, R2.Pin_0
  N2: Part1.A1, R3.wiper
  N3: Part1.D9_PWM, LED1.anode
  N4: Part1.5V, R1.pin_0, R3.leg1
  N5: Part1.GND, R2.Pin_1, R3.leg2, R4.Pin_1
  N6: LED1.cathode, R4.Pin_0
